# Fritzing sketch epd_vddonly (saved by Fritzing 0.9.3b)
circuit board: 7.87cm x 8.12cm
breadboards: 1

parts:
  pyboard1 = Micro Python pyboard [part_number=PYBv10b]
  R1 = Resistor [tolerance=±5% resistance=1M package=THT]
  J1 = double row male pin header, 14 pins [form="♂ (male)"]
  J4 = female pin header, 2 pins [form="♀ (female)"]
  IC1 = IC, DIP package, 14 pins [chip_label=IC]
  J5 = female pin header, 4 pins [form="♀ (female)"]
  J3 = female pin header, 2 pins [form="♀ (female)"]
  Q1 = PNP-Transistor [part_number=LP0701N3 package="TO92 [THT]"]
  J6 = female pin header, 8 pins [form="♀ (female)"]
  J7 = female pin header, 5 pins [form="♀ (female)"]
  J8 = female pin header, 8 pins [form="♀ (female)"]
  R4 = Resistor [tolerance=±5% resistance=100 package=THT]
  R3 = Resistor [tolerance=±5% resistance=2.2k package=THT]
  R2 = Resistor [tolerance=±5% resistance=1M package=THT]
  J2 = female pin header, 2 pins [form="♀ (female)"]
  C1 = Ceramic Capacitor [capacitance=1µF package="200 mil [THT, multilayer]"]
  Batt1 = LilyPad Coin Cell Battery Holder

nets:
  N1: pyboard1.X4, J6.pin7
  N2: pyboard1.X5, J6.pin6
  N3: pyboard1.X6, J6.pin5
  N4: pyboard1.X7, J6.pin3
  N5: pyboard1.X8, J6.pin4
  N6: pyboard1.X9, IC1.pin11
  N7: pyboard1.X10, IC1.pin8
  N8: pyboard1.X11, J1.pin4
  N9: pyboard1.X12, J1.pin11
  gnd: pyboard1.X14_GND, pyboard1.Y14_GND, J1.pin1, J4.pin2, IC1.pin7, J3.pin2, J6.pin1, J7.pin3, J8.pin2, R3.Pin_0, R2.Pin_1, J2.pin2, C1.0, Batt1.-
  3v3: pyboard1.X15_3V3, R1.Pin_1, IC1.pin14, Q1.s, J2.pin1, Batt1.+
  vin: pyboard1.X16_VIN, J3.pin1
  N10: pyboard1.Y1, J1.pin6
  N11: pyboard1.Y2, J1.pin9
  N12: pyboard1.Y3, J1.pin7
  N13: pyboard1.Y4, J1.pin8
  N14: pyboard1.Y5, J1.pin12
  N15: pyboard1.Y6, J1.pin2
  N16: pyboard1.Y7, J1.pin3
  N17: pyboard1.Y8, J1.pin13
  N18: pyboard1.Y9, IC1.pin4
  N19: pyboard1.Y10, IC1.pin1
  N20: pyboard1.Y11, R1.Pin_0, Q1.g
  N21: pyboard1.Y12, IC1.pin5, IC1.pin6, IC1.pin12, IC1.pin13, R2.Pin_0
  N22: J1.pin5, IC1.pin10, J5.pin3
  N23: J1.pin10, IC1.pin9, J5.pin4
  vdd: J1.pin14, J4.pin1, Q1.d, J6.pin8, J7.pin2, R4.Pin_0, R3.Pin_1
  N24: IC1.pin2, J5.pin2, J7.pin5, J8.pin5
  N25: IC1.pin3, J5.pin1, J7.pin4, J8.pin4
  N26: J8.pin1, R4.Pin_1, C1.1

notes:
  Vin
  Gnd
  Vdd
  Vdd (sw)
  X scl
  X sda
  scl
  sda
  Y scl
  Y sda
  74HC4066N
  x
  y
  NRF24L01
  BMP180
  FRAM
  vcc
  gnd
  wp
  a2
  a1
  a0
  io
  vdd
  ce
  csn
  sck
  mosi
  miso
  irq
  ssn
  pwron
  pwron\
  wp (nc)
  nc
  io (nc)
  I2C
  3V3
  EPD
  R3, R4 optional to meet FRAM Vcc slew rate limit (PCB has 10uF)
  *
  * Optional

custom parts:
  PNP-Transistor: P-channel MOSFET small signal transistor
